// Logisim project project.circ as structural Verilog
module MUX_2 (
  input  in_1,
  input  in_2,
  input  in_3,
  output out_4
);

  wire and_1_out, and_2_out, not_1_out;

  not not_1 (not_1_out, in_3);
  and and_1 (and_1_out, in_1, in_3);
  and and_2 (and_2_out, in_2, not_1_out);
  or or_1 (out_4, and_1_out, and_2_out);
endmodule

module MUX_2_3 (
  input  in_1,
  input  in_2,
  input  in_3,
  output out_4
);

  wire not_1_out;

  not not_1 (not_1_out, in_3);
  assign out_4 = in_3 ? in_1 : 1'bz;  // Controlled_Buffer controlled_buffer_1
  assign out_4 = not_1_out ? in_2 : 1'bz;  // Controlled_Buffer controlled_buffer_2
endmodule

module MUX_4 (
  input  in_1,
  input  in_2,
  input  in_3,
  input  in_4,
  input  in_5,
  input  in_6,
  output out_7
);

  wire multiplexer_1_out, multiplexer_2_out;

  Multiplexer multiplexer_1 (.in0(in_1), .in1(in_2), .out(multiplexer_1_out), .sel(in_5));
  Multiplexer multiplexer_2 (.in0(in_3), .in1(in_4), .out(multiplexer_2_out), .sel(in_5));
  Multiplexer multiplexer_3 (.in0(multiplexer_1_out), .in1(multiplexer_2_out), .out(out_7), .sel(in_6));
endmodule

module Encoder_83 (
  input  in_1,
  input  in_2,
  input  in_3,
  input  in_4,
  input  in_5,
  input  in_6,
  input  in_7,
  input  in_8,
  output out_9,
  output out_10,
  output out_11
);

  or or_1 (out_9, in_8, in_7, in_6, in_5);
  or or_2 (out_10, in_8, in_7, in_4, in_3);
  or or_3 (out_11, in_8, in_6, in_4, in_2);
endmodule

module PreEncoder_83 (
  input  in_1,
  input  in_2,
  input  in_3,
  input  in_4,
  input  in_5,
  input  in_6,
  input  in_7,
  input  in_8,
  output out_9,
  output out_10,
  output out_11
);

  wire and_1_out, and_2_out, and_3_out, and_4_out, and_5_out, and_6_out, and_7_out, nor_1_out, nor_2_out,
       not_1_out, not_2_out, not_3_out, not_4_out, not_5_out;

  and and_1 (and_1_out, not_1_out, in_7);
  not not_1 (not_1_out, in_8);
  not not_2 (not_2_out, and_1_out);
  and and_2 (and_2_out, not_2_out, not_1_out, in_6);
  not not_3 (not_3_out, and_2_out);
  and and_3 (and_3_out, not_3_out, not_2_out, not_1_out, in_5);
  nor nor_1 (nor_1_out, in_8, and_1_out, and_2_out, and_3_out);
  and and_4 (and_4_out, nor_1_out, in_4);
  not not_4 (not_4_out, and_4_out);
  and and_5 (and_5_out, not_4_out, nor_1_out, in_3);
  not not_5 (not_5_out, and_5_out);
  and and_6 (and_6_out, nor_2_out, nor_1_out, in_1);
  and and_7 (and_7_out, not_5_out, not_4_out, nor_1_out, in_2);
  nor nor_2 (nor_2_out, nor_1_out, and_4_out, and_5_out, and_7_out);
  or or_1 (out_9, and_7_out, and_4_out, and_2_out, in_8);
  or or_2 (out_10, and_5_out, and_4_out, and_1_out, in_8);
  or or_3 (out_11, and_3_out, and_2_out, and_1_out, in_8);
endmodule

module Decoder_38 (
  input  in_1,
  input  in_2,
  input  in_3,
  output out_4,
  output out_5,
  output out_6,
  output out_7,
  output out_8,
  output out_9,
  output out_10,
  output out_11
);

  wire not_1_out, not_2_out, not_3_out;

  not not_1 (not_1_out, in_1);
  not not_2 (not_2_out, in_2);
  not not_3 (not_3_out, in_3);
  and and_1 (out_4, not_1_out, not_2_out, not_3_out);
  and and_2 (out_5, in_1, not_2_out, not_3_out);
  and and_3 (out_6, not_1_out, in_2, not_3_out);
  and and_4 (out_7, in_1, in_2, not_3_out);
  and and_5 (out_8, not_1_out, not_2_out, in_3);
  and and_6 (out_9, in_1, not_2_out, in_3);
  and and_7 (out_10, not_1_out, in_2, in_3);
  and and_8 (out_11, in_1, in_2, in_3);
endmodule

module SR_Latch (
  input  S,
  input  R,
  output out_3,
  output Q
);

  wire or_1_out, or_2_out;

  or or_1 (or_1_out, S, Q);
  or or_2 (or_2_out, out_3, R);
  not not_1 (out_3, or_1_out);
  not not_2 (Q, or_2_out);
endmodule

module D_Latch (
  input  CLK,
  input  D,
  output out_3,
  output Q
);

  wire and_1_out, and_2_out, not_1_out;

  not not_1 (not_1_out, D);
  and and_1 (and_1_out, CLK, D);
  and and_2 (and_2_out, CLK, not_1_out);
  SR_Latch sr_latch_1 (.S(and_1_out), .R(and_2_out), .out_3(out_3), .Q(Q));
endmodule

module D_Trigger (
  input  CLK,
  input  RST,
  input  D,
  input  EN,
  output out_5,
  output Q
);

  wire and_1_out, and_2_out, d_latch_1_q, multiplexer_1_out, not_1_out, not_2_out, or_1_out, or_2_out;

  not not_1 (not_1_out, RST);
  Multiplexer multiplexer_1 (.in0(Q), .in1(D), .out(multiplexer_1_out), .sel(EN));
  or or_1 (or_1_out, RST, not_2_out);
  not not_2 (not_2_out, CLK);
  and and_1 (and_1_out, multiplexer_1_out, not_1_out);
  or or_2 (or_2_out, RST, CLK);
  and and_2 (and_2_out, d_latch_1_q, not_1_out);
  D_Latch d_latch_1 (.CLK(or_1_out), .D(and_1_out), .Q(d_latch_1_q));  // open: out_3
  D_Latch d_latch_2 (.CLK(or_2_out), .D(and_2_out), .out_3(out_5), .Q(Q));
endmodule

module Register_4 (
  input  [3:0] D_in,
  input  EN,
  input  RST,
  input  CLK,
  output [3:0] D_out
);

  D_Trigger d_trigger_1 (.CLK(CLK), .RST(RST), .D(D_in[0]), .EN(EN), .Q(D_out[0]));  // open: out_5
  D_Trigger d_trigger_2 (.CLK(CLK), .RST(RST), .D(D_in[1]), .EN(EN), .Q(D_out[1]));  // open: out_5
  D_Trigger d_trigger_3 (.CLK(CLK), .RST(RST), .D(D_in[2]), .EN(EN), .Q(D_out[2]));  // open: out_5
  D_Trigger d_trigger_4 (.CLK(CLK), .RST(RST), .D(D_in[3]), .EN(EN), .Q(D_out[3]));  // open: out_5
endmodule

module Register_8 (
  input  [1:0] S,
  input  [7:0] D_in,
  input  RST,
  input  CLK,
  input  Algor,
  output [7:0] D_out
);

  wire multiplexer_1_out, multiplexer_2_out, multiplexer_3_out, multiplexer_4_out, multiplexer_5_out,
       multiplexer_6_out, multiplexer_7_out, multiplexer_8_out, multiplexer_9_out;

  Multiplexer multiplexer_1 (.in0(1'b0), .in1(D_out[7]), .out(multiplexer_1_out), .sel(Algor));
  Multiplexer #(.select(2)) multiplexer_2 (
    .in0(D_out[0]), .in1(D_out[1]), .in2(1'b0), .in3(D_in[0]), .out(multiplexer_2_out), .sel(S));
  Multiplexer #(.select(2)) multiplexer_3 (
    .in0(D_out[1]), .in1(D_out[2]), .in2(D_out[0]), .in3(D_in[1]), .out(multiplexer_3_out), .sel(S));
  Multiplexer #(.select(2)) multiplexer_4 (
    .in0(D_out[2]), .in1(D_out[3]), .in2(D_out[1]), .in3(D_in[2]), .out(multiplexer_4_out), .sel(S));
  Multiplexer #(.select(2)) multiplexer_5 (
    .in0(D_out[3]), .in1(D_out[4]), .in2(D_out[2]), .in3(D_in[3]), .out(multiplexer_5_out), .sel(S));
  Multiplexer #(.select(2)) multiplexer_6 (
    .in0(D_out[4]), .in1(D_out[5]), .in2(D_out[3]), .in3(D_in[4]), .out(multiplexer_6_out), .sel(S));
  Multiplexer #(.select(2)) multiplexer_7 (
    .in0(D_out[5]), .in1(D_out[6]), .in2(D_out[4]), .in3(D_in[5]), .out(multiplexer_7_out), .sel(S));
  Multiplexer #(.select(2)) multiplexer_8 (
    .in0(D_out[6]), .in1(D_out[7]), .in2(D_out[5]), .in3(D_in[6]), .out(multiplexer_8_out), .sel(S));
  Multiplexer #(.select(2)) multiplexer_9 (
    .in0(D_out[7]), .in1(multiplexer_1_out), .in2(D_out[6]), .in3(D_in[7]), .out(multiplexer_9_out), .sel(S));
  D_Trigger d_trigger_1 (.CLK(CLK), .RST(RST), .D(multiplexer_2_out), .EN(1'b1), .Q(D_out[0]));  // open: out_5
  D_Trigger d_trigger_2 (.CLK(CLK), .RST(RST), .D(multiplexer_3_out), .EN(1'b1), .Q(D_out[1]));  // open: out_5
  D_Trigger d_trigger_3 (.CLK(CLK), .RST(RST), .D(multiplexer_4_out), .EN(1'b1), .Q(D_out[2]));  // open: out_5
  D_Trigger d_trigger_4 (.CLK(CLK), .RST(RST), .D(multiplexer_5_out), .EN(1'b1), .Q(D_out[3]));  // open: out_5
  D_Trigger d_trigger_5 (.CLK(CLK), .RST(RST), .D(multiplexer_6_out), .EN(1'b1), .Q(D_out[4]));  // open: out_5
  D_Trigger d_trigger_6 (.CLK(CLK), .RST(RST), .D(multiplexer_7_out), .EN(1'b1), .Q(D_out[5]));  // open: out_5
  D_Trigger d_trigger_7 (.CLK(CLK), .RST(RST), .D(multiplexer_8_out), .EN(1'b1), .Q(D_out[6]));  // open: out_5
  D_Trigger d_trigger_8 (.CLK(CLK), .RST(RST), .D(multiplexer_9_out), .EN(1'b1), .Q(D_out[7]));  // open: out_5
endmodule

module Counter_44 (
  input  RST,
  input  CLK,
  output [7:0] CNT
);

  wire comparator_1_eq, or_1_out;
  wire [7:0] adder_1_out;

  or or_1 (or_1_out, RST, comparator_1_eq);
  Adder adder_1 (.a(CNT), .b(8'h1), .out(adder_1_out));  // open: cin, cout
  Register_8 register_8_1 (.S(2'b11), .D_in(adder_1_out), .RST(or_1_out), .CLK(CLK), .Algor(1'b0), .D_out(CNT));
  Comparator comparator_1 (.a(CNT), .b(8'h2c), .eq(comparator_1_eq));  // open: gt, lt
endmodule

module Detech_01 (
  input  CLK,
  input  RST,
  input  A,
  output Y
);

  wire and_1_out, d_trigger_1_q, not_1_out;

  not not_1 (not_1_out, A);
  and and_1 (and_1_out, d_trigger_1_q, A);
  D_Trigger d_trigger_1 (.CLK(CLK), .RST(RST), .D(not_1_out), .EN(1'b1), .Q(d_trigger_1_q));  // open: out_5
  D_Trigger d_trigger_2 (.CLK(CLK), .RST(RST), .D(and_1_out), .EN(1'b1), .Q(Y));  // open: out_5
endmodule
